// Logisim project Basic_comp.circ as structural Verilog: 33 circuits, main circuit main
module main (
  output [7:0] out_1
);

  wire ac_ctr_1_clr_ac, ac_ctr_1_inc_ac, ac_ctr_1_ld, ar_ctr_1_clr, ar_ctr_1_inr, ar_ctr_1_ld, CLK,
       clock_1_out, dr_ctr_1_inc, dr_ctr_1_ld, E, E_OUT, FGI, FGO, I, IEN, ir_ctr_1_ld, memory_ctr_1_read,
       memory_ctr_1_write, not_1_out, not_2_out, outr_ctr_1_ld, pc_ctr_1_clr, pc_ctr_1_inc, pc_ctr_1_ld, R,
       S, sc_ctr_1_clr, tr_ctr_1_ld;
  wire [2:0] bus_ctr_1_select;
  wire [3:0] SC;
  wire [6:0] ALU_CTR;
  wire [7:0] INPR;
  wire [11:0] AR;
  wire [15:0] AC, alu_16bits_1_outp, BUS_OUT, DR, IR, P_counter_output, ram_1_dout, TMP_R_output;
  wire [15:12] AD_R_output;

  SC_CTR sc_ctr_1 (.IR(IR), .R(R), .I(I), .Seq(SC), .clr(sc_ctr_1_clr));
  R_CTR r_ctr_1 (.CLK(CLK), .Seq(SC), .IEN(IEN), .FGO(FGO), .FGI(FGI), .R(R));
  Counter #(.max('hf), .width(4)) counter_1 (
    .load(sc_ctr_1_clr), .D(4'b0000), .count(not_1_out), .Q(SC), .clk(CLK));  // open: carry, up, clr
  not not_1 (not_1_out, sc_ctr_1_clr);
  ALU_16Bits alu_16bits_1 (
    .SHR(ALU_CTR[5]), .SHL(ALU_CTR[6]), .AND(ALU_CTR[0]), .ADD(ALU_CTR[1]), .DR(ALU_CTR[2]),
    .INPR(ALU_CTR[3]), .COM(ALU_CTR[4]), .AC(AC), .DataRegister(DR), .E_in(E), .InputRegister(INPR),
    .E_out(E_OUT), .OUTP(alu_16bits_1_outp));
  OUTR_CTR outr_ctr_1 (.I(I), .Seq(SC), .IR(IR), .LD(outr_ctr_1_ld));
  Memory_CTR memory_ctr_1 (.I(I), .R(R), .Seq(SC), .IR(IR), .write(memory_ctr_1_write), .read(memory_ctr_1_read));
  // Probe on alu_16bits_1_outp
  INP_R inp_r_1 (.out_1(INPR));
  I_CTR i_ctr_1 (.IR15(IR[15]), .R(R), .Seq(SC), .CLK(CLK), .I(I));
  S_CTR s_ctr_1 (.Seq(SC), .IR(IR), .CLK(CLK), .I(I), .S(S));
  TR_CTR tr_ctr_1 (.Seq(SC), .R(R), .LD(tr_ctr_1_ld));
  RAM #(.addrWidth(12), .asyncread("true"), .dataWidth(16)) ram_1 (
    .addr(AR), .we(memory_ctr_1_write), .oe(memory_ctr_1_read), .clk(CLK), .din(BUS_OUT), .dout(ram_1_dout));
  DR_CTR dr_ctr_1 (.Seq(SC), .IR(IR), .INC(dr_ctr_1_inc), .LD(dr_ctr_1_ld));
  AC_CTR ac_ctr_1 (
    .I(I), .Seq(SC), .IR(IR), .LD(ac_ctr_1_ld), .CTRL(ALU_CTR), .INC_AC(ac_ctr_1_inc_ac),
    .CLR_AC(ac_ctr_1_clr_ac));
  IR_CTR ir_ctr_1 (.R(R), .Seq(SC), .LD(ir_ctr_1_ld));
  // Probe on out_1
  OUTR_c outr_c_1 (.INPUT(BUS_OUT), .LD(outr_ctr_1_ld), .Clock(CLK), .OUTPUT(out_1));
  AR_CTR ar_ctr_1 (.Seq(SC), .I(I), .R(R), .IR(IR), .INR(ar_ctr_1_inr), .CLR(ar_ctr_1_clr), .LD(ar_ctr_1_ld));
  PC_CTR pc_ctr_1 (
    .AC(AC), .DR(DR), .FGO(FGO), .FGI(FGI), .E(E), .I(I), .R(R), .Seq(SC), .IR(IR), .CLR(pc_ctr_1_clr),
    .LD(pc_ctr_1_ld), .INC(pc_ctr_1_inc));
  TR_c TMP_R (.INPUT(BUS_OUT), .LD(tr_ctr_1_ld), .Clock(CLK), .OUTPUT(TMP_R_output));  // open: CLR
  DR_c DATA_R (.INPUT(BUS_OUT), .LD(dr_ctr_1_ld), .INC(dr_ctr_1_inc), .Clock(CLK), .OUTPUT(DR));  // open: CLR
  AC_c ACC (
    .INPUT(alu_16bits_1_outp), .LD(ac_ctr_1_ld), .INC(ac_ctr_1_inc_ac), .Clock(CLK), .CLR(ac_ctr_1_clr_ac),
    .OUTPUT(AC));
  IR_c INS_R (.INPUT(BUS_OUT), .LD(ir_ctr_1_ld), .CLK(CLK), .OUTPUT(IR));
  IEN_CTR ien_ctr_1 (.Seq(SC), .IR(IR), .CLK(CLK), .R(R), .I(I), .IEN(IEN));
  FGO_CTR fgo_ctr_1 (.Seq(SC), .IR(IR), .CLK(CLK), .I(I), .FGO(FGO));
  AR_c AD_R (
    .INPUT(BUS_OUT), .LD(ar_ctr_1_ld), .INC(ar_ctr_1_inr), .Clock(CLK), .CLR(ar_ctr_1_clr),
    .OUTPUT({AD_R_output, AR}));
  // Probe on P_counter_output
  PC P_counter (
    .INPUT(BUS_OUT), .LD(pc_ctr_1_ld), .INC(pc_ctr_1_inc), .Clock(CLK), .CLR(pc_ctr_1_clr),
    .OUTPUT(P_counter_output));
  // Probe on ram_1_dout
  // Probe on DR
  // Probe on AC
  // Probe on IR
  // Probe on TMP_R_output
  BUS_CTR bus_ctr_1 (.I(I), .R(R), .Seq(SC), .IR(IR), .Select(bus_ctr_1_select));
  // Probe on bus_ctr_1_select
  // Probe on {AD_R_output, AR}
  E_CTR e_ctr_1 (.Seq(SC), .IR(IR), .E_out(E_OUT), .I(I), .R(R), .Clock(CLK), .AC(AC), .E(E));
  FGI_CTR fgi_ctr_1 (.Seq(SC), .IR(IR), .CLK(CLK), .INPUT(INPR), .I(I), .FGI(FGI));
  BUS_CIR bus_cir_1 (
    .RAM(ram_1_dout), .DR(DR), .AC(AC), .IR(IR), .TR(TMP_R_output), .AR({AD_R_output, AR}),
    .PC(P_counter_output), .SEL(bus_ctr_1_select), .Output(BUS_OUT));
  Clock clock_1 (.out(clock_1_out));
  and and_1 (CLK, clock_1_out, not_2_out);
  not not_2 (not_2_out, S);
  // Probe on BUS_OUT

  // Other names for the same wires on the sheet: IR_15 = IR[15]
endmodule

// BUS
module BUS_CIR (
  input  [15:0] RAM,
  input  [15:0] DR,
  input  [15:0] AC,
  input  [15:0] IR,
  input  [2:0] SEL,
  input  [15:0] TR,
  input  [15:0] AR,
  input  [15:0] PC,
  output [15:0] Output
);

  Multiplexer #(.disabled("Z"), .enable("true"), .select(3), .width(16)) multiplexer_1 (
    .in0({16{1'b0}}), .in1(AR), .in2(PC), .in3(DR), .in4(AC), .in5(IR), .in6(TR), .in7(RAM), .out(Output),
    .sel(SEL));  // open: en
endmodule

module BUS_CTR (
  input  R,
  input  I,
  input  [15:0] IR,
  input  [3:0] Seq,
  output [2:0] Select
);

  wire and_1_out, and_2_out, and_3_out, and_4_out, and_5_out, and_6_out, and_7_out, and_8_out, and_9_out,
       and_12_out, and_13_out, and_14_out, and_15_out, and_16_out, and_17_out, D0, D1, D2, D3, D4, D5, D6,
       D7, not_1_out, not_2_out, not_3_out, not_4_out, not_5_out, p, r_t, T0, T1, T2, T3, T4, T5, T6, T7, T8,
       T9, T10, T11, T12, T13, T14, T15, X1, X2, X3, X4, X5, X6, X7;

  and and_1 (and_1_out, T4, D4);
  and and_2 (and_2_out, T5, D5);
  not not_1 (not_1_out, R);
  and and_3 (and_3_out, not_1_out, T0);
  and and_4 (and_4_out, R, T0);
  and and_5 (and_5_out, T5, D2);
  and and_6 (and_6_out, T6, D6);
  and and_7 (and_7_out, T4, D3);
  and and_8 (and_8_out, p, IR[10]);
  or or_1 (X1, and_1_out, and_2_out);
  and and_9 (and_9_out, T4, D5);
  or or_2 (X3, and_5_out, and_6_out);
  or or_3 (X4, and_7_out, and_8_out);
  or or_4 (X2, and_3_out, and_9_out, and_4_out);
  not not_2 (not_2_out, R);
  and and_10 (X5, not_2_out, T2);
  and and_11 (X6, R, T1);
  not not_3 (not_3_out, R);
  not not_4 (not_4_out, D7);
  and and_12 (and_12_out, not_4_out, I, T3);
  and and_13 (and_13_out, not_3_out, T1);
  and and_14 (and_14_out, D0, T4);
  and and_15 (and_15_out, D1, T4);
  and and_16 (and_16_out, D2, T4);
  and and_17 (and_17_out, D6, T4);
  or or_5 (X7, and_13_out, and_14_out, and_15_out, and_12_out, and_16_out, and_17_out, r_t);
  Priority_Encoder priority_encoder_1 (
    .in0(1'b0), .in1(X1), .in2(X2), .in3(X3), .in4(X4), .in5(X5), .in6(X6), .in7(X7), .out(Select));  // open: en_in, gs, en_out
  not not_5 (not_5_out, I);
  and and_18 (r_t, D7, not_5_out, T3);
  and and_19 (p, D7, I, T3);
  Decoder #(.disabled("Z"), .select(3)) decoder_1 (
    .out0(D0), .out1(D1), .out2(D2), .out3(D3), .out4(D4), .out5(D5), .out6(D6), .out7(D7), .sel(IR[14:12]));  // open: en
  Decoder #(.disabled("Z"), .select(4)) decoder_2 (
    .out0(T0), .out1(T1), .out2(T2), .out3(T3), .out4(T4), .out5(T5), .out6(T6), .out7(T7), .out8(T8),
    .out9(T9), .out10(T10), .out11(T11), .out12(T12), .out13(T13), .out14(T14), .out15(T15), .sel(Seq));  // open: en

  // Other names for the same wires on the sheet: B0 = IR[0]; B1 = IR[1]; B2 = IR[2]; B3 = IR[3]; B4 = IR[4];
  //   B5 = IR[5]; B6 = IR[6]; B7 = IR[7]; B8 = IR[8]; B9 = IR[9]; B10 = IR[10]; B11 = IR[11]; IR_15 = IR[15]
endmodule

module FA (
  input  C_i,
  input  A_i,
  input  B_i,
  output sum_i,
  output carry_i
);

  wire and_1_out, and_2_out, xor_1_out;

  xor xor_1 (xor_1_out, A_i, B_i);
  and and_1 (and_1_out, A_i, B_i);
  xor xor_2 (sum_i, C_i, xor_1_out);
  and and_2 (and_2_out, C_i, xor_1_out);
  or or_1 (carry_i, and_2_out, and_1_out);
endmodule

module Adder_12bits (
  input  cin,
  input  [11:0] A,
  input  [11:0] B,
  output cout,
  output [11:0] sum
);

  wire fa_1_carry_i, fa_2_carry_i, fa_3_carry_i, fa_4_carry_i, fa_5_carry_i, fa_6_carry_i, fa_7_carry_i,
       fa_8_carry_i, fa_9_carry_i, fa_10_carry_i, fa_11_carry_i;

  FA fa_1 (.C_i(cin), .A_i(A[0]), .B_i(B[0]), .sum_i(sum[0]), .carry_i(fa_1_carry_i));
  FA fa_2 (.C_i(fa_1_carry_i), .A_i(A[1]), .B_i(B[1]), .sum_i(sum[1]), .carry_i(fa_2_carry_i));
  FA fa_3 (.C_i(fa_2_carry_i), .A_i(A[2]), .B_i(B[2]), .sum_i(sum[2]), .carry_i(fa_3_carry_i));
  FA fa_4 (.C_i(fa_3_carry_i), .A_i(A[3]), .B_i(B[3]), .sum_i(sum[3]), .carry_i(fa_4_carry_i));
  FA fa_5 (.C_i(fa_4_carry_i), .A_i(A[4]), .B_i(B[4]), .sum_i(sum[4]), .carry_i(fa_5_carry_i));
  FA fa_6 (.C_i(fa_5_carry_i), .A_i(A[5]), .B_i(B[5]), .sum_i(sum[5]), .carry_i(fa_6_carry_i));
  FA fa_7 (.C_i(fa_6_carry_i), .A_i(A[6]), .B_i(B[6]), .sum_i(sum[6]), .carry_i(fa_7_carry_i));
  FA fa_8 (.C_i(fa_7_carry_i), .A_i(A[7]), .B_i(B[7]), .sum_i(sum[7]), .carry_i(fa_8_carry_i));
  FA fa_9 (.C_i(fa_8_carry_i), .A_i(A[8]), .B_i(B[8]), .sum_i(sum[8]), .carry_i(fa_9_carry_i));
  FA fa_10 (.C_i(fa_9_carry_i), .A_i(A[9]), .B_i(B[9]), .sum_i(sum[9]), .carry_i(fa_10_carry_i));
  FA fa_11 (.C_i(fa_10_carry_i), .A_i(A[10]), .B_i(B[10]), .sum_i(sum[10]), .carry_i(fa_11_carry_i));
  FA fa_12 (.C_i(fa_11_carry_i), .A_i(A[11]), .B_i(B[11]), .sum_i(sum[11]), .carry_i(cout));
endmodule

module Adder_16bits (
  input  [15:0] A,
  input  Cin,
  input  [15:0] B,
  output cout,
  output [15:0] sum
);

  wire adder_12bits_1_cout, fa_1_carry_i, fa_2_carry_i, fa_3_carry_i;

  Adder_12bits adder_12bits_1 (.A(B[11:0]), .B(A[11:0]), .cin(Cin), .cout(adder_12bits_1_cout), .sum(sum[11:0]));
  FA fa_1 (.C_i(adder_12bits_1_cout), .A_i(A[12]), .B_i(B[12]), .sum_i(sum[12]), .carry_i(fa_1_carry_i));
  FA fa_2 (.C_i(fa_1_carry_i), .A_i(A[13]), .B_i(B[13]), .sum_i(sum[13]), .carry_i(fa_2_carry_i));
  FA fa_3 (.C_i(fa_2_carry_i), .A_i(A[14]), .B_i(B[14]), .sum_i(sum[14]), .carry_i(fa_3_carry_i));
  FA fa_4 (.C_i(fa_3_carry_i), .A_i(A[15]), .B_i(B[15]), .sum_i(sum[15]), .carry_i(cout));

  // Other names for the same wires on the sheet: a_12[11:0] = A[11:0]; b_12[11:0] = B[11:0]; S[11:0] = sum[11:0]
endmodule

module AR_c (
  input  LD,
  input  [15:0] INPUT,
  input  CLR,
  input  INC,
  input  Clock,
  output [15:0] OUTPUT
);

  Counter #(.max('hfff), .width(12)) counter_1 (
    .load(LD), .D(INPUT[11:0]), .count(INC), .Q(OUTPUT[11:0]), .clk(Clock), .clr(CLR));  // open: carry, up

  assign OUTPUT[15:12] = 4'b0000;
endmodule

module AR_CTR (
  input  R,
  input  I,
  input  [15:0] IR,
  input  [3:0] Seq,
  output LD,
  output CLR,
  output INR
);

  wire and_1_out, and_2_out, and_3_out, D0, D1, D2, D3, D4, D5, D6, D7, not_1_out, not_2_out, not_3_out, T0,
       T1, T2, T3, T4, T5, T6, T7, T8, T9, T10, T11, T12, T13, T14, T15;

  Decoder #(.disabled("Z"), .select(4)) decoder_1 (
    .out0(T0), .out1(T1), .out2(T2), .out3(T3), .out4(T4), .out5(T5), .out6(T6), .out7(T7), .out8(T8),
    .out9(T9), .out10(T10), .out11(T11), .out12(T12), .out13(T13), .out14(T14), .out15(T15), .sel(Seq),
    .en(1'b1));
  Decoder #(.disabled("Z"), .select(3)) decoder_2 (
    .out0(D0), .out1(D1), .out2(D2), .out3(D3), .out4(D4), .out5(D5), .out6(D6), .out7(D7), .sel(IR[14:12]));  // open: en
  not not_1 (not_1_out, R);
  not not_2 (not_2_out, R);
  not not_3 (not_3_out, D7);
  and and_1 (and_1_out, T0, not_1_out);
  and and_2 (and_2_out, T2, not_2_out);
  and and_3 (and_3_out, I, T3, not_3_out);
  and and_4 (CLR, R, T0);
  and and_5 (INR, D5, T4);
  or or_1 (LD, and_1_out, and_2_out, and_3_out);

  // Other names for the same wires on the sheet: B0 = IR[0]; B1 = IR[1]; B2 = IR[2]; B3 = IR[3]; B4 = IR[4];
  //   B5 = IR[5]; B6 = IR[6]; B7 = IR[7]; B8 = IR[8]; B9 = IR[9]; B10 = IR[10]; B11 = IR[11]; IR_15 = IR[15]
endmodule

module DR_c (
  input  LD,
  input  [15:0] INPUT,
  input  INC,
  input  CLR,
  input  Clock,
  output [15:0] OUTPUT
);

  Counter #(.max('hffff), .width(16)) counter_1 (
    .load(LD), .D(INPUT), .count(INC), .Q(OUTPUT), .clk(Clock), .clr(CLR));  // open: carry, up
endmodule

module DR_CTR (
  input  [15:0] IR,
  input  [3:0] Seq,
  output LD,
  output INC
);

  wire and_1_out, and_2_out, and_3_out, and_4_out, D0, D1, D2, D3, D4, D5, D6, D7, T0, T1, T2, T3, T4, T5,
       T6, T7, T8, T9, T10, T11, T12, T13, T14, T15;

  Decoder #(.disabled("Z"), .select(4)) decoder_1 (
    .out0(T0), .out1(T1), .out2(T2), .out3(T3), .out4(T4), .out5(T5), .out6(T6), .out7(T7), .out8(T8),
    .out9(T9), .out10(T10), .out11(T11), .out12(T12), .out13(T13), .out14(T14), .out15(T15), .sel(Seq));  // open: en
  Decoder #(.disabled("Z"), .select(3)) decoder_2 (
    .out0(D0), .out1(D1), .out2(D2), .out3(D3), .out4(D4), .out5(D5), .out6(D6), .out7(D7), .sel(IR[14:12]));  // open: en
  and and_1 (and_1_out, D0, T4);
  and and_2 (and_2_out, D1, T4);
  and and_3 (and_3_out, D2, T4);
  and and_4 (and_4_out, D6, T4);
  and and_5 (INC, D6, T5);
  or or_1 (LD, and_1_out, and_2_out, and_3_out, and_4_out);

  // Other names for the same wires on the sheet: B0 = IR[0]; B1 = IR[1]; B2 = IR[2]; B3 = IR[3]; B4 = IR[4];
  //   B5 = IR[5]; B6 = IR[6]; B7 = IR[7]; B8 = IR[8]; B9 = IR[9]; B10 = IR[10]; B11 = IR[11]; IR_15 = IR[15]
endmodule

module IR_c (
  input  LD,
  input  [15:0] INPUT,
  input  CLK,
  output [15:0] OUTPUT
);

  Counter #(.max('hffff), .width(16)) counter_1 (
    .load(LD), .D(INPUT), .count(1'b0), .Q(OUTPUT), .clk(CLK));  // open: carry, up, clr
endmodule

module IR_CTR (
  input  [3:0] Seq,
  input  R,
  output LD
);

  wire not_1_out, T0, T1, T2, T3, T4, T5, T6, T7, T8, T9, T10, T11, T12, T13, T14, T15;

  not not_1 (not_1_out, R);
  and and_1 (LD, not_1_out, T1);
  Decoder #(.disabled("Z"), .select(4)) decoder_1 (
    .out0(T0), .out1(T1), .out2(T2), .out3(T3), .out4(T4), .out5(T5), .out6(T6), .out7(T7), .out8(T8),
    .out9(T9), .out10(T10), .out11(T11), .out12(T12), .out13(T13), .out14(T14), .out15(T15), .sel(Seq));  // open: en
endmodule

module TR_c (
  input  LD,
  input  [15:0] INPUT,
  input  CLR,
  input  Clock,
  output [15:0] OUTPUT
);

  Counter #(.max('hffff), .width(16)) counter_1 (
    .load(LD), .D(INPUT), .count(1'b0), .Q(OUTPUT), .clk(Clock), .clr(CLR));  // open: carry, up
endmodule

module TR_CTR (
  input  [3:0] Seq,
  input  R,
  output LD
);

  wire T0, T1, T2, T3, T4, T5, T6, T7, T8, T9, T10, T11, T12, T13, T14, T15;

  and and_1 (LD, R, T0);
  Decoder #(.disabled("Z"), .select(4)) decoder_1 (
    .out0(T0), .out1(T1), .out2(T2), .out3(T3), .out4(T4), .out5(T5), .out6(T6), .out7(T7), .out8(T8),
    .out9(T9), .out10(T10), .out11(T11), .out12(T12), .out13(T13), .out14(T14), .out15(T15), .sel(Seq));  // open: en
endmodule

module PC (
  input  LD,
  input  [15:0] INPUT,
  input  CLR,
  input  INC,
  input  Clock,
  output [15:0] OUTPUT
);

  Counter #(.max('hfff), .width(12)) counter_1 (
    .load(LD), .D(INPUT[11:0]), .count(INC), .Q(OUTPUT[11:0]), .clk(Clock), .clr(CLR));  // open: carry, up

  assign OUTPUT[15:12] = 4'b0000;
endmodule

module PC_CTR (
  input  [15:0] IR,
  input  FGO,
  input  FGI,
  input  E,
  input  I,
  input  R,
  input  [3:0] Seq,
  input  [15:0] AC,
  input  [15:0] DR,
  output INC,
  output CLR,
  output LD
);

  wire AC_t, and_4_out, and_5_out, and_6_out, and_7_out, and_8_out, and_9_out, and_10_out, and_11_out,
       and_12_out, and_13_out, and_14_out, D0, D1, D2, D3, D4, D5, D6, D7, DR_t, not_1_out, not_2_out,
       not_3_out, not_4_out, not_5_out, not_6_out, p, r_t, T0, T1, T2, T3, T4, T5, T6, T7, T8, T9, T10, T11,
       T12, T13, T14, T15;

  not not_1 (not_1_out, I);
  and and_1 (p, D7, I, T3);
  and and_2 (r_t, D7, not_1_out, T3);
  not not_2 (not_2_out, AC_t);
  or or_1 (AC_t, AC[0], AC[1], AC[2], AC[3], AC[4], AC[5], AC[6], AC[7], AC[8], AC[9], AC[10], AC[11], AC[12], AC[13], AC[14], AC[15]);
  or or_2 (DR_t, DR[0], DR[1], DR[2], DR[3], DR[4], DR[5], DR[6], DR[7], DR[8], DR[9], DR[10], DR[11], DR[12], DR[13], DR[14], DR[15]);
  not not_3 (not_3_out, R);
  not not_4 (not_4_out, DR_t);
  not not_5 (not_5_out, AC[15]);
  not not_6 (not_6_out, E);
  and and_3 (CLR, R, T1);
  and and_4 (and_4_out, D4, T4);
  and and_5 (and_5_out, D5, T5);
  and and_6 (and_6_out, not_3_out, T1);
  and and_7 (and_7_out, R, T2);
  and and_8 (and_8_out, D6, T6, not_4_out);
  and and_9 (and_9_out, r_t, IR[4], not_5_out);
  and and_10 (and_10_out, r_t, IR[3], AC[15]);
  and and_11 (and_11_out, r_t, IR[2], not_2_out);
  and and_12 (and_12_out, r_t, IR[1], not_6_out);
  and and_13 (and_13_out, p, IR[9], FGI);
  and and_14 (and_14_out, p, FGO);
  Decoder #(.disabled("Z"), .select(3)) decoder_1 (
    .out0(D0), .out1(D1), .out2(D2), .out3(D3), .out4(D4), .out5(D5), .out6(D6), .out7(D7), .sel(IR[14:12]));  // open: en
  or or_3 (LD, and_4_out, and_5_out);
  or or_4 (INC, and_6_out, and_7_out, and_8_out, and_9_out, and_10_out, and_11_out, and_12_out, and_13_out, and_14_out);
  Decoder #(.disabled("Z"), .select(4)) decoder_2 (
    .out0(T0), .out1(T1), .out2(T2), .out3(T3), .out4(T4), .out5(T5), .out6(T6), .out7(T7), .out8(T8),
    .out9(T9), .out10(T10), .out11(T11), .out12(T12), .out13(T13), .out14(T14), .out15(T15), .sel(Seq));  // open: en

  // Other names for the same wires on the sheet: AC_15 = AC[15]; B0 = IR[0]; B1 = IR[1]; B2 = IR[2]; B3 = IR[3];
  //   B4 = IR[4]; B5 = IR[5]; B6 = IR[6]; B7 = IR[7]; B8 = IR[8]; B9 = IR[9]; B10 = IR[10]; B11 = IR[11];
  //   IR_15 = IR[15]
endmodule

module OUTR_CTR (
  input  I,
  input  [15:0] IR,
  input  [3:0] Seq,
  output LD
);

  wire D0, D1, D2, D3, D4, D5, D6, D7, p, T0, T1, T2, T3, T4, T5, T6, T7, T8, T9, T10, T11, T12, T13, T14,
       T15;

  Decoder #(.disabled("Z"), .select(3)) decoder_1 (
    .out0(D0), .out1(D1), .out2(D2), .out3(D3), .out4(D4), .out5(D5), .out6(D6), .out7(D7), .sel(IR[14:12]));  // open: en
  and and_1 (LD, p, IR[10]);
  Decoder #(.disabled("Z"), .select(4)) decoder_2 (
    .out0(T0), .out1(T1), .out2(T2), .out3(T3), .out4(T4), .out5(T5), .out6(T6), .out7(T7), .out8(T8),
    .out9(T9), .out10(T10), .out11(T11), .out12(T12), .out13(T13), .out14(T14), .out15(T15), .sel(Seq));  // open: en
  and and_2 (p, D7, I, T3);

  // Other names for the same wires on the sheet: B0 = IR[0]; B1 = IR[1]; B2 = IR[2]; B3 = IR[3]; B4 = IR[4];
  //   B5 = IR[5]; B6 = IR[6]; B7 = IR[7]; B8 = IR[8]; B9 = IR[9]; B10 = IR[10]; B11 = IR[11]; IR_15 = IR[15]
endmodule

module AC_c (
  input  LD,
  input  [15:0] INPUT,
  input  INC,
  input  CLR,
  input  Clock,
  output [15:0] OUTPUT
);

  Counter #(.max('hffff), .width(16)) counter_1 (
    .load(LD), .D(INPUT), .count(INC), .Q(OUTPUT), .clk(Clock), .clr(CLR));  // open: carry, up
endmodule

module AC_CTR (
  input  I,
  input  [15:0] IR,
  input  [3:0] Seq,
  output LD,
  output [6:0] CTRL,
  output INC_AC,
  output CLR_AC
);

  wire and_1_out, and_2_out, and_3_out, and_4_out, and_5_out, and_6_out, D0, D1, D2, D3, D4, D5, D6, D7,
       not_1_out, p, r, SHR_out, T0, T1, T2, T3, T4, T5, T6, T7, T8, T9, T10, T11, T12, T13, T14, T15;

  Decoder #(.disabled("Z"), .select(3)) decoder_1 (
    .out0(D0), .out1(D1), .out2(D2), .out3(D3), .out4(D4), .out5(D5), .out6(D6), .out7(D7), .sel(IR[14:12]));  // open: en
  Decoder #(.disabled("Z"), .select(4)) decoder_2 (
    .out0(T0), .out1(T1), .out2(T2), .out3(T3), .out4(T4), .out5(T5), .out6(T6), .out7(T7), .out8(T8),
    .out9(T9), .out10(T10), .out11(T11), .out12(T12), .out13(T13), .out14(T14), .out15(T15), .sel(Seq),
    .en(1'b1));
  not not_1 (not_1_out, I);
  and and_1 (and_1_out, D0, T5);
  and and_2 (and_2_out, T5, D1);
  and and_3 (and_3_out, T5, D2);
  and and_4 (and_4_out, p, IR[11]);
  and and_5 (and_5_out, r, IR[9]);
  and SHR (SHR_out, r, IR[7]);
  and and_6 (and_6_out, r, IR[6]);
  and INC (INC_AC, r, IR[5]);
  and CLR (CLR_AC, r, IR[11]);
  and and_7 (r, D7, not_1_out, T3);
  or or_1 (LD, and_1_out, and_2_out, and_3_out, and_4_out, and_5_out, SHR_out, and_6_out);
  and and_8 (p, D7, I, T3);
  and AND_9 (CTRL[0], D0, T5);
  and ADD (CTRL[1], T5, D1);
  and DR (CTRL[2], T5, D2);
  and INPR (CTRL[3], p, IR[11]);
  and COM (CTRL[4], r, IR[9]);
  and and_10 (CTRL[5], r, IR[7]);
  and SHL (CTRL[6], r, IR[6]);

  // Other names for the same wires on the sheet: B0 = IR[0]; B1 = IR[1]; B2 = IR[2]; B3 = IR[3]; B4 = IR[4];
  //   B5 = IR[5]; B6 = IR[6]; B7 = IR[7]; B8 = IR[8]; B9 = IR[9]; B10 = IR[10]; B11 = IR[11]; IR_15 = IR[15]
endmodule

// ALU
module ALU_1Bit (
  input  [6:0] INPUT_CTR,
  input  AC_i,
  input  DR_i,
  input  C_i,
  input  INPR_i,
  input  AC_iplus1,
  input  AC_i_1,
  output C_1,
  output I_i_a1a8e7c9
);

  wire ADD_out, AND_out, COM_out, DR_out, fa_1_sum_i, INPR_out, not_1_out, SHL_out, SHR_out;

  FA fa_1 (.C_i(C_i), .A_i(AC_i), .B_i(DR_i), .sum_i(fa_1_sum_i), .carry_i(C_1));
  not not_1 (not_1_out, AC_i);
  and AND (AND_out, INPUT_CTR[6], AC_i, DR_i);
  and ADD (ADD_out, INPUT_CTR[5], fa_1_sum_i);
  and DR (DR_out, INPUT_CTR[4], DR_i);
  and INPR (INPR_out, INPUT_CTR[3], INPR_i);
  and COM (COM_out, INPUT_CTR[2], not_1_out);
  and SHR (SHR_out, INPUT_CTR[1], AC_iplus1);
  and SHL (SHL_out, INPUT_CTR[0], AC_i_1);
  or or_1 (I_i_a1a8e7c9, AND_out, ADD_out, DR_out, INPR_out, COM_out, SHR_out, SHL_out);
endmodule

// ALU
module ALU_16Bits (
  input  E_in,
  input  [15:0] DataRegister,
  input  [7:0] InputRegister,
  input  [15:0] AC,
  input  AND,
  input  ADD,
  input  DR,
  input  INPR,
  input  COM,
  input  SHR,
  input  SHL,
  output [15:0] OUTP,
  output E_out
);

  wire alu_1bit_1_c_1, alu_1bit_2_c_1, alu_1bit_3_c_1, alu_1bit_4_c_1, alu_1bit_5_c_1, alu_1bit_6_c_1,
       alu_1bit_7_c_1, alu_1bit_8_c_1, alu_1bit_9_c_1, alu_1bit_10_c_1, alu_1bit_11_c_1, alu_1bit_12_c_1,
       alu_1bit_13_c_1, alu_1bit_14_c_1, alu_1bit_15_c_1, and_1_out, and_2_out, and_3_out, and_4_out, C_16,
       nor_1_out;

  nor nor_1 (nor_1_out, SHR, ADD, SHL);
  and and_1 (and_1_out, AC[15], SHL);
  and and_2 (and_2_out, AC[0], SHR);
  and and_3 (and_3_out, ADD, C_16);
  and and_4 (and_4_out, E_in, nor_1_out);
  or or_1 (E_out, and_1_out, and_2_out, and_3_out, and_4_out);
  ALU_1Bit alu_1bit_1 (
    .DR_i(DataRegister[0]), .C_i(1'b0), .AC_i(AC[0]), .INPR_i(InputRegister[0]), .AC_iplus1(AC[1]),
    .AC_i_1(E_in), .INPUT_CTR({AND, ADD, DR, INPR, COM, SHR, SHL}), .I_i_a1a8e7c9(OUTP[0]),
    .C_1(alu_1bit_1_c_1));
  ALU_1Bit alu_1bit_2 (
    .DR_i(DataRegister[1]), .C_i(alu_1bit_1_c_1), .AC_i(AC[1]), .INPR_i(InputRegister[1]), .AC_iplus1(AC[2]),
    .AC_i_1(AC[0]), .INPUT_CTR({AND, ADD, DR, INPR, COM, SHR, SHL}), .I_i_a1a8e7c9(OUTP[1]),
    .C_1(alu_1bit_2_c_1));
  ALU_1Bit alu_1bit_3 (
    .DR_i(DataRegister[2]), .C_i(alu_1bit_2_c_1), .AC_i(AC[2]), .INPR_i(InputRegister[2]), .AC_iplus1(AC[3]),
    .AC_i_1(AC[1]), .INPUT_CTR({AND, ADD, DR, INPR, COM, SHR, SHL}), .I_i_a1a8e7c9(OUTP[2]),
    .C_1(alu_1bit_3_c_1));
  ALU_1Bit alu_1bit_4 (
    .DR_i(DataRegister[3]), .C_i(alu_1bit_3_c_1), .AC_i(AC[3]), .INPR_i(InputRegister[3]), .AC_iplus1(AC[4]),
    .AC_i_1(AC[2]), .INPUT_CTR({AND, ADD, DR, INPR, COM, SHR, SHL}), .I_i_a1a8e7c9(OUTP[3]),
    .C_1(alu_1bit_4_c_1));
  ALU_1Bit alu_1bit_5 (
    .DR_i(DataRegister[4]), .C_i(alu_1bit_4_c_1), .AC_i(AC[4]), .INPR_i(InputRegister[4]), .AC_iplus1(AC[5]),
    .AC_i_1(AC[3]), .INPUT_CTR({AND, ADD, DR, INPR, COM, SHR, SHL}), .I_i_a1a8e7c9(OUTP[4]),
    .C_1(alu_1bit_5_c_1));
  ALU_1Bit alu_1bit_6 (
    .DR_i(DataRegister[5]), .C_i(alu_1bit_5_c_1), .AC_i(AC[5]), .INPR_i(InputRegister[5]), .AC_iplus1(AC[6]),
    .AC_i_1(AC[4]), .INPUT_CTR({AND, ADD, DR, INPR, COM, SHR, SHL}), .I_i_a1a8e7c9(OUTP[5]),
    .C_1(alu_1bit_6_c_1));
  ALU_1Bit alu_1bit_7 (
    .DR_i(DataRegister[6]), .C_i(alu_1bit_6_c_1), .AC_i(AC[6]), .INPR_i(InputRegister[6]), .AC_iplus1(AC[7]),
    .AC_i_1(AC[5]), .INPUT_CTR({AND, ADD, DR, INPR, COM, SHR, SHL}), .I_i_a1a8e7c9(OUTP[6]),
    .C_1(alu_1bit_7_c_1));
  ALU_1Bit alu_1bit_8 (
    .DR_i(DataRegister[7]), .C_i(alu_1bit_7_c_1), .AC_i(AC[7]), .INPR_i(InputRegister[7]), .AC_iplus1(AC[8]),
    .AC_i_1(AC[6]), .INPUT_CTR({AND, ADD, DR, INPR, COM, SHR, SHL}), .I_i_a1a8e7c9(OUTP[7]),
    .C_1(alu_1bit_8_c_1));
  ALU_1Bit alu_1bit_9 (
    .DR_i(DataRegister[8]), .C_i(alu_1bit_8_c_1), .AC_i(AC[8]), .INPR_i(1'b0), .AC_iplus1(AC[9]),
    .AC_i_1(AC[7]), .INPUT_CTR({AND, ADD, DR, INPR, COM, SHR, SHL}), .I_i_a1a8e7c9(OUTP[8]),
    .C_1(alu_1bit_9_c_1));
  ALU_1Bit alu_1bit_10 (
    .DR_i(DataRegister[9]), .C_i(alu_1bit_9_c_1), .AC_i(AC[9]), .INPR_i(1'b0), .AC_iplus1(AC[10]),
    .AC_i_1(AC[8]), .INPUT_CTR({AND, ADD, DR, INPR, COM, SHR, SHL}), .I_i_a1a8e7c9(OUTP[9]),
    .C_1(alu_1bit_10_c_1));
  ALU_1Bit alu_1bit_11 (
    .DR_i(DataRegister[10]), .C_i(alu_1bit_10_c_1), .AC_i(AC[10]), .INPR_i(1'b0), .AC_iplus1(AC[11]),
    .AC_i_1(AC[9]), .INPUT_CTR({AND, ADD, DR, INPR, COM, SHR, SHL}), .I_i_a1a8e7c9(OUTP[10]),
    .C_1(alu_1bit_11_c_1));
  ALU_1Bit alu_1bit_12 (
    .DR_i(DataRegister[11]), .C_i(alu_1bit_11_c_1), .AC_i(AC[11]), .INPR_i(1'b0), .AC_iplus1(AC[12]),
    .AC_i_1(AC[10]), .INPUT_CTR({AND, ADD, DR, INPR, COM, SHR, SHL}), .I_i_a1a8e7c9(OUTP[11]),
    .C_1(alu_1bit_12_c_1));
  ALU_1Bit alu_1bit_13 (
    .DR_i(DataRegister[12]), .C_i(alu_1bit_12_c_1), .AC_i(AC[12]), .INPR_i(1'b0), .AC_iplus1(AC[13]),
    .AC_i_1(AC[11]), .INPUT_CTR({AND, ADD, DR, INPR, COM, SHR, SHL}), .I_i_a1a8e7c9(OUTP[12]),
    .C_1(alu_1bit_13_c_1));
  ALU_1Bit alu_1bit_14 (
    .DR_i(DataRegister[13]), .C_i(alu_1bit_13_c_1), .AC_i(AC[13]), .INPR_i(1'b0), .AC_iplus1(AC[14]),
    .AC_i_1(AC[12]), .INPUT_CTR({AND, ADD, DR, INPR, COM, SHR, SHL}), .I_i_a1a8e7c9(OUTP[13]),
    .C_1(alu_1bit_14_c_1));
  ALU_1Bit alu_1bit_15 (
    .DR_i(DataRegister[14]), .C_i(alu_1bit_14_c_1), .AC_i(AC[14]), .INPR_i(1'b0), .AC_iplus1(AC[15]),
    .AC_i_1(AC[13]), .INPUT_CTR({AND, ADD, DR, INPR, COM, SHR, SHL}), .I_i_a1a8e7c9(OUTP[14]),
    .C_1(alu_1bit_15_c_1));
  ALU_1Bit alu_1bit_16 (
    .DR_i(DataRegister[15]), .C_i(alu_1bit_15_c_1), .AC_i(AC[15]), .INPR_i(1'b0), .AC_iplus1(E_in),
    .AC_i_1(AC[14]), .INPUT_CTR({AND, ADD, DR, INPR, COM, SHR, SHL}), .I_i_a1a8e7c9(OUTP[15]), .C_1(C_16));

  // Other names for the same wires on the sheet: AC_0 = AC[0]; AC_1 = AC[1]; AC_2 = AC[2]; AC_3 = AC[3]; AC_4 = AC[4];
  //   AC_5 = AC[5]; AC_6 = AC[6]; AC_7 = AC[7]; AC_8 = AC[8]; AC_9 = AC[9]; AC_10 = AC[10]; AC_11 = AC[11];
  //   AC_12 = AC[12]; AC_13 = AC[13]; AC_14 = AC[14]; AC_15 = AC[15];
  //   CTR_Gates[6:0] = {AND, ADD, DR, INPR, COM, SHR, SHL}; DR0 = DataRegister[0]; DR1 = DataRegister[1];
  //   DR2 = DataRegister[2]; DR3 = DataRegister[3]; DR4 = DataRegister[4]; DR5 = DataRegister[5];
  //   DR6 = DataRegister[6]; DR7 = DataRegister[7]; DR8 = DataRegister[8]; DR9 = DataRegister[9];
  //   DR10 = DataRegister[10]; DR11 = DataRegister[11]; DR12 = DataRegister[12]; DR13 = DataRegister[13];
  //   DR14 = DataRegister[14]; DR15 = DataRegister[15]; IN0 = InputRegister[0]; IN1 = InputRegister[1];
  //   IN2 = InputRegister[2]; IN3 = InputRegister[3]; IN4 = InputRegister[4]; IN5 = InputRegister[5];
  //   IN6 = InputRegister[6]; IN7 = InputRegister[7]; I0 = OUTP[0]; I1 = OUTP[1]; I2 = OUTP[2]; I3 = OUTP[3];
  //   I4 = OUTP[4]; I5 = OUTP[5]; I6 = OUTP[6]; I7 = OUTP[7]; I8 = OUTP[8]; I9 = OUTP[9]; I10 = OUTP[10];
  //   I11 = OUTP[11]; I12 = OUTP[12]; I13 = OUTP[13]; I14 = OUTP[14]; I15 = OUTP[15]
endmodule

module INP_R (
  output [7:0] out_1
);

  Register register_1 (.en(1'b0), .Q(out_1));  // open: D, clk, clr
endmodule

// Memory
module Memory_CTR (
  input  [3:0] Seq,
  input  I,
  input  R,
  input  [15:0] IR,
  output write,
  output read
);

  wire and_1_out, and_2_out, and_3_out, and_4_out, and_5_out, and_6_out, and_7_out, and_8_out, and_9_out,
       and_10_out, D0, D1, D2, D3, D4, D5, D6, D7, not_1_out, not_2_out, T0, T1, T2, T3, T4, T5, T6, T7, T8,
       T9, T10, T11, T12, T13, T14, T15;

  Decoder #(.disabled("Z"), .select(3)) decoder_1 (
    .out0(D0), .out1(D1), .out2(D2), .out3(D3), .out4(D4), .out5(D5), .out6(D6), .out7(D7), .sel(IR[14:12]));  // open: en
  Decoder #(.disabled("Z"), .select(4)) decoder_2 (
    .out0(T0), .out1(T1), .out2(T2), .out3(T3), .out4(T4), .out5(T5), .out6(T6), .out7(T7), .out8(T8),
    .out9(T9), .out10(T10), .out11(T11), .out12(T12), .out13(T13), .out14(T14), .out15(T15), .sel(Seq));  // open: en
  and and_1 (and_1_out, R, T1);
  and and_2 (and_2_out, D3, T4);
  and and_3 (and_3_out, D5, T4);
  and and_4 (and_4_out, D6, T6);
  or or_1 (write, and_1_out, and_2_out, and_3_out, and_4_out);
  not not_1 (not_1_out, R);
  not not_2 (not_2_out, D7);
  and and_5 (and_5_out, not_1_out, T1);
  and and_6 (and_6_out, D0, T4);
  and and_7 (and_7_out, D1, T4);
  and and_8 (and_8_out, D2, T4);
  and and_9 (and_9_out, I, not_2_out, T3);
  and and_10 (and_10_out, D6, T4);
  or or_2 (read, and_5_out, and_6_out, and_7_out, and_8_out, and_9_out, and_10_out);

  // Other names for the same wires on the sheet: B0 = IR[0]; B1 = IR[1]; B2 = IR[2]; B3 = IR[3]; B4 = IR[4];
  //   B5 = IR[5]; B6 = IR[6]; B7 = IR[7]; B8 = IR[8]; B9 = IR[9]; B10 = IR[10]; B11 = IR[11]; IR_15 = IR[15]
endmodule

// E_c
module E_CTR (
  input  [15:0] AC,
  input  Clock,
  input  E_out,
  input  I,
  input  R,
  input  [15:0] IR,
  input  [3:0] Seq,
  output E
);

  wire and_1_out, and_2_out, and_3_out, and_4_out, D0, D1, D2, D3, D4, D5, D6, D7, not_1_out, not_2_out,
       not_3_out, or_1_out, or_2_out, or_3_out, r_t, T0, T1, T2, T3, T4, T5, T6, T7, T8, T9, T10, T11, T12,
       T13, T14, T15;

  Decoder #(.disabled("Z"), .select(3)) decoder_1 (
    .out0(D0), .out1(D1), .out2(D2), .out3(D3), .out4(D4), .out5(D5), .out6(D6), .out7(D7), .sel(IR[14:12]));  // open: en
  and and_1 (and_1_out, r_t, IR[8]);
  and and_2 (and_2_out, r_t, IR[10]);
  or or_1 (or_1_out, and_2_out, and_1_out);
  Decoder #(.disabled("Z"), .select(4)) decoder_2 (
    .out0(T0), .out1(T1), .out2(T2), .out3(T3), .out4(T4), .out5(T5), .out6(T6), .out7(T7), .out8(T8),
    .out9(T9), .out10(T10), .out11(T11), .out12(T12), .out13(T13), .out14(T14), .out15(T15), .sel(Seq));  // open: en
  not not_1 (not_1_out, or_1_out);
  not not_2 (not_2_out, E_out);
  not not_3 (not_3_out, I);
  and and_3 (and_3_out, E_out, not_1_out);
  and and_4 (and_4_out, not_2_out, not_1_out);
  and and_5 (r_t, D7, not_3_out, T3);
  or or_2 (or_2_out, and_3_out, and_1_out);
  or or_3 (or_3_out, and_4_out, and_1_out, and_2_out);
  J_K_Flip_Flop j_k_ff_1 (.J(or_2_out), .clk(Clock), .K(or_3_out), .Q(E));  // open: Qn, preset, reset

  // Other names for the same wires on the sheet: AC_0 = AC[0]; AC_1 = AC[1]; AC_2 = AC[2]; AC_3 = AC[3]; AC_4 = AC[4];
  //   AC_5 = AC[5]; AC_6 = AC[6]; AC_7 = AC[7]; AC_8 = AC[8]; AC_9 = AC[9]; AC_10 = AC[10]; AC_11 = AC[11];
  //   AC_12 = AC[12]; AC_13 = AC[13]; AC_14 = AC[14]; AC_15 = AC[15]; B0 = IR[0]; B1 = IR[1]; B2 = IR[2]; B3 = IR[3];
  //   B4 = IR[4]; B5 = IR[5]; B6 = IR[6]; B7 = IR[7]; B8 = IR[8]; B9 = IR[9]; B10 = IR[10]; B11 = IR[11];
  //   IR_15 = IR[15]
endmodule

// FGI_c
module FGI_CTR (
  input  CLK,
  input  I,
  input  [7:0] INPUT,
  input  [15:0] IR,
  input  [3:0] Seq,
  output FGI
);

  wire and_2_out, D0, D1, D2, D3, D4, D5, D6, D7, INPR, p, T0, T1, T2, T3, T4, T5, T6, T7, T8, T9, T10, T11,
       T12, T13, T14, T15;

  Decoder #(.select(3)) decoder_1 (
    .out0(D0), .out1(D1), .out2(D2), .out3(D3), .out4(D4), .out5(D5), .out6(D6), .out7(D7), .sel(IR[14:12]));  // open: en
  and and_1 (p, D7, I, T3);
  Decoder #(.disabled("Z"), .select(4)) decoder_2 (
    .out0(T0), .out1(T1), .out2(T2), .out3(T3), .out4(T4), .out5(T5), .out6(T6), .out7(T7), .out8(T8),
    .out9(T9), .out10(T10), .out11(T11), .out12(T12), .out13(T13), .out14(T14), .out15(T15), .sel(Seq),
    .en(1'b1));
  and and_2 (and_2_out, p, IR[11]);
  J_K_Flip_Flop j_k_ff_1 (.J(INPR), .clk(CLK), .K(and_2_out), .Q(FGI));  // open: Qn, preset, reset
  or or_1 (INPR, INPUT[0], INPUT[1], INPUT[2], INPUT[3], INPUT[4], INPUT[5], INPUT[6], INPUT[7]);

  // Other names for the same wires on the sheet: B0 = IR[0]; B1 = IR[1]; B2 = IR[2]; B3 = IR[3]; B4 = IR[4];
  //   B5 = IR[5]; B6 = IR[6]; B7 = IR[7]; B8 = IR[8]; B9 = IR[9]; B10 = IR[10]; B11 = IR[11]; IR_15 = IR[15]
endmodule

// FGO_c
module FGO_CTR (
  input  CLK,
  input  I,
  input  [15:0] IR,
  input  [3:0] Seq,
  output FGO
);

  wire and_2_out, D0, D1, D2, D3, D4, D5, D6, D7, p, T0, T1, T2, T3, T4, T5, T6, T7, T8, T9, T10, T11, T12,
       T13, T14, T15;

  Decoder #(.select(3)) decoder_1 (
    .out0(D0), .out1(D1), .out2(D2), .out3(D3), .out4(D4), .out5(D5), .out6(D6), .out7(D7), .sel(IR[14:12]));  // open: en
  and and_1 (p, D7, I, T3);
  Decoder #(.disabled("Z"), .select(4)) decoder_2 (
    .out0(T0), .out1(T1), .out2(T2), .out3(T3), .out4(T4), .out5(T5), .out6(T6), .out7(T7), .out8(T8),
    .out9(T9), .out10(T10), .out11(T11), .out12(T12), .out13(T13), .out14(T14), .out15(T15), .sel(Seq),
    .en(1'b1));
  and and_2 (and_2_out, p, IR[10]);
  J_K_Flip_Flop j_k_ff_1 (.J(1'b0), .K(and_2_out), .clk(CLK), .Q(FGO));  // open: Qn, preset, reset

  // Other names for the same wires on the sheet: B0 = IR[0]; B1 = IR[1]; B2 = IR[2]; B3 = IR[3]; B4 = IR[4];
  //   B5 = IR[5]; B6 = IR[6]; B7 = IR[7]; B8 = IR[8]; B9 = IR[9]; B10 = IR[10]; B11 = IR[11]; IR_15 = IR[15]
endmodule

// IEN_c
module IEN_CTR (
  input  CLK,
  input  R,
  input  I,
  input  [15:0] IR,
  input  [3:0] Seq,
  output IEN
);

  wire and_2_out, and_3_out, and_4_out, D0, D1, D2, D3, D4, D5, D6, D7, or_1_out, p, T0, T1, T2, T3, T4, T5,
       T6, T7, T8, T9, T10, T11, T12, T13, T14, T15;

  Decoder #(.select(3)) decoder_1 (
    .out0(D0), .out1(D1), .out2(D2), .out3(D3), .out4(D4), .out5(D5), .out6(D6), .out7(D7), .sel(IR[14:12]));  // open: en
  and and_1 (p, D7, I, T3);
  Decoder #(.disabled("Z"), .select(4)) decoder_2 (
    .out0(T0), .out1(T1), .out2(T2), .out3(T3), .out4(T4), .out5(T5), .out6(T6), .out7(T7), .out8(T8),
    .out9(T9), .out10(T10), .out11(T11), .out12(T12), .out13(T13), .out14(T14), .out15(T15), .sel(Seq));  // open: en
  and and_2 (and_2_out, p, IR[7]);
  and and_3 (and_3_out, p, IR[6]);
  and and_4 (and_4_out, R, T2);
  or or_1 (or_1_out, and_3_out, and_4_out);
  J_K_Flip_Flop j_k_ff_1 (.J(and_2_out), .clk(CLK), .K(or_1_out), .Q(IEN));  // open: Qn, preset, reset

  // Other names for the same wires on the sheet: B0 = IR[0]; B1 = IR[1]; B2 = IR[2]; B3 = IR[3]; B4 = IR[4];
  //   B5 = IR[5]; B6 = IR[6]; B7 = IR[7]; B8 = IR[8]; B9 = IR[9]; B10 = IR[10]; B11 = IR[11]; IR_15 = IR[15]
endmodule

// S_c
module S_CTR (
  input  CLK,
  input  I,
  input  [15:0] IR,
  input  [3:0] Seq,
  output S
);

  wire and_2_out, D0, D1, D2, D3, D4, D5, D6, D7, not_1_out, r, T0, T1, T2, T3, T4, T5, T6, T7, T8, T9, T10,
       T11, T12, T13, T14, T15;

  Decoder #(.select(3)) decoder_1 (
    .out0(D0), .out1(D1), .out2(D2), .out3(D3), .out4(D4), .out5(D5), .out6(D6), .out7(D7), .sel(IR[14:12]));  // open: en
  not not_1 (not_1_out, I);
  and and_1 (r, D7, not_1_out, T3);
  Decoder #(.disabled("Z"), .select(4)) decoder_2 (
    .out0(T0), .out1(T1), .out2(T2), .out3(T3), .out4(T4), .out5(T5), .out6(T6), .out7(T7), .out8(T8),
    .out9(T9), .out10(T10), .out11(T11), .out12(T12), .out13(T13), .out14(T14), .out15(T15), .sel(Seq));  // open: en
  and and_2 (and_2_out, r, IR[0]);
  J_K_Flip_Flop j_k_ff_1 (.J(and_2_out), .clk(CLK), .K(1'b0), .Q(S));  // open: Qn, preset, reset

  // Other names for the same wires on the sheet: B0 = IR[0]; B1 = IR[1]; B2 = IR[2]; B3 = IR[3]; B4 = IR[4];
  //   B5 = IR[5]; B6 = IR[6]; B7 = IR[7]; B8 = IR[8]; B9 = IR[9]; B10 = IR[10]; B11 = IR[11]; IR_15 = IR[15]
endmodule

// I_c
module I_CTR (
  input  IR15,
  input  R,
  input  [3:0] Seq,
  input  CLK,
  output I
);

  wire and_1_out, multiplexer_1_out, not_1_out, T0, T1, T2, T3, T4, T5, T6, T7, T8, T9, T10, T11, T12, T13,
       T14, T15;

  not not_1 (not_1_out, R);
  Decoder #(.disabled("Z"), .select(4)) decoder_1 (
    .out0(T0), .out1(T1), .out2(T2), .out3(T3), .out4(T4), .out5(T5), .out6(T6), .out7(T7), .out8(T8),
    .out9(T9), .out10(T10), .out11(T11), .out12(T12), .out13(T13), .out14(T14), .out15(T15), .sel(Seq),
    .en(1'b1));
  Multiplexer #(.disabled("Z")) multiplexer_1 (.in0(I), .in1(IR15), .out(multiplexer_1_out), .sel(and_1_out));
  and and_1 (and_1_out, not_1_out, T2);
  D_Flip_Flop d_ff_1 (.clk(CLK), .D(multiplexer_1_out), .Q(I));  // open: Qn, preset, reset
endmodule

// R_c
module R_CTR (
  input  CLK,
  input  IEN,
  input  FGO,
  input  FGI,
  input  [3:0] Seq,
  output R
);

  wire and_1_out, and_2_out, nor_1_out, or_1_out, T0, T1, T2, T3, T4, T5, T6, T7, T8, T9, T10, T11, T12, T13,
       T14, T15;

  or or_1 (or_1_out, FGI, FGO);
  and and_1 (and_1_out, R, T2);
  Decoder #(.disabled("Z"), .select(4)) decoder_1 (
    .out0(T0), .out1(T1), .out2(T2), .out3(T3), .out4(T4), .out5(T5), .out6(T6), .out7(T7), .out8(T8),
    .out9(T9), .out10(T10), .out11(T11), .out12(T12), .out13(T13), .out14(T14), .out15(T15), .sel(Seq));  // open: en
  nor nor_1 (nor_1_out, T0, T1, T2);
  and and_2 (and_2_out, nor_1_out, IEN, or_1_out);
  J_K_Flip_Flop j_k_ff_1 (.J(and_2_out), .clk(CLK), .K(and_1_out), .Q(R));  // open: Qn, preset, reset
endmodule

// SC_c
module SC_CTR (
  input  [15:0] IR,
  input  [3:0] Seq,
  input  I,
  input  R,
  output clr
);

  wire and_1_out, and_2_out, and_3_out, and_4_out, and_5_out, and_6_out, and_7_out, and_8_out, D0, D1, D2,
       D3, D4, D5, D6, D7, not_1_out, p, r_t, T0, T1, T2, T3, T4, T5, T6, T7, T8, T9, T10, T11, T12, T13,
       T14, T15;

  not not_1 (not_1_out, I);
  and and_1 (and_1_out, R, T2);
  and and_2 (and_2_out, D0, T5);
  and and_3 (and_3_out, D1, T5);
  and and_4 (and_4_out, D2, T5);
  and and_5 (and_5_out, D3, T4);
  and and_6 (and_6_out, D4, T4);
  and and_7 (and_7_out, D5, T5);
  and and_8 (and_8_out, D6, T6);
  and and_9 (r_t, D7, not_1_out, T3);
  and and_10 (p, D7, I, T3);
  or or_1 (clr, and_1_out, and_2_out, and_3_out, and_4_out, and_5_out, and_6_out, and_7_out, and_8_out, r_t, p);
  Decoder #(.disabled("Z"), .select(3)) decoder_1 (
    .out0(D0), .out1(D1), .out2(D2), .out3(D3), .out4(D4), .out5(D5), .out6(D6), .out7(D7), .sel(IR[14:12]));  // open: en
  Decoder #(.disabled("Z"), .select(4)) decoder_2 (
    .out0(T0), .out1(T1), .out2(T2), .out3(T3), .out4(T4), .out5(T5), .out6(T6), .out7(T7), .out8(T8),
    .out9(T9), .out10(T10), .out11(T11), .out12(T12), .out13(T13), .out14(T14), .out15(T15), .sel(Seq));  // open: en

  // Other names for the same wires on the sheet: B0 = IR[0]; B1 = IR[1]; B2 = IR[2]; B3 = IR[3]; B4 = IR[4];
  //   B5 = IR[5]; B6 = IR[6]; B7 = IR[7]; B8 = IR[8]; B9 = IR[9]; B10 = IR[10]; B11 = IR[11]; IR_15 = IR[15]
endmodule

// OUTR
module OUTR_c (
  input  LD,
  input  [15:0] INPUT,
  input  Clock,
  output [7:0] OUTPUT
);

  Counter counter_1 (.load(LD), .D(INPUT[7:0]), .count(1'b0), .Q(OUTPUT), .clk(Clock));  // open: carry, up, clr
endmodule

module ALU_0 (
  input  [6:0] INPUT_CTR,
  input  AC_i,
  input  DR_i,
  input  C_i,
  input  INPR_i,
  input  AC_iplus1,
  input  AC_i_1,
  output C_1,
  output I_i_a1a8e7c9
);

  wire ADD_out, AND_out, COM_out, DR_out, fa_1_sum_i, INPR_out, not_1_out, SHL_out, SHR_out;

  FA fa_1 (.C_i(C_i), .A_i(AC_i), .B_i(DR_i), .sum_i(fa_1_sum_i), .carry_i(C_1));
  not not_1 (not_1_out, AC_i);
  and AND (AND_out, INPUT_CTR[6], AC_i, DR_i);
  and ADD (ADD_out, INPUT_CTR[5], fa_1_sum_i);
  and DR (DR_out, INPUT_CTR[4], DR_i);
  and INPR (INPR_out, INPUT_CTR[3], INPR_i);
  and COM (COM_out, INPUT_CTR[2], not_1_out);
  and SHR (SHR_out, INPUT_CTR[1], AC_iplus1);
  and SHL (SHL_out, INPUT_CTR[0], AC_i_1);
  or or_1 (I_i_a1a8e7c9, AND_out, ADD_out, DR_out, INPR_out, COM_out, SHR_out, SHL_out);
endmodule
